// Logisim project Additionneur.circ as structural Verilog: 2 circuits, main circuit main
// Half
module DemiAdditionneur (
  input  e0,
  input  e1,
  output s,
  output r
);

  wire and_1_out, and_2_out, not_1_out, not_2_out;

  not not_1 (not_1_out, e0);
  not not_2 (not_2_out, e1);
  and and_1 (and_1_out, not_1_out, e1);
  or or_1 (s, and_1_out, and_2_out);
  and and_2 (and_2_out, e0, not_2_out);
  and and_3 (r, e0, e1);
endmodule

module main (
  input  r0,
  input  e0,
  input  e1,
  output s,
  output r
);

  wire demiadditionneur_1_r, demiadditionneur_1_s, demiadditionneur_2_r;

  DemiAdditionneur demiadditionneur_1 (.e0(e0), .e1(e1), .s(demiadditionneur_1_s), .r(demiadditionneur_1_r));
  DemiAdditionneur demiadditionneur_2 (.e0(r0), .e1(demiadditionneur_1_s), .s(s), .r(demiadditionneur_2_r));
  or or_1 (r, demiadditionneur_2_r, demiadditionneur_1_r);

  // Notes on the sheet:
  //   s0
  //   r1
  //   r2
endmodule
