// Logisim project Additionneur2.circ as structural Verilog: 1 circuit, main circuit main
module main (
  input  e0,
  input  e1,
  input  r0,
  output s,
  output r
);

  wire and_1_out, and_2_out, and_3_out, and_4_out, and_5_out, and_6_out, and_7_out, not_1_out, not_2_out,
       not_3_out, not_4_out, not_5_out, not_6_out, not_7_out, not_8_out;

  not not_1 (not_1_out, e0);
  not not_2 (not_2_out, e1);
  not not_3 (not_3_out, e0);
  not not_4 (not_4_out, e1);
  and and_1 (and_1_out, not_3_out, not_4_out, r0);
  not not_5 (not_5_out, e0);
  and and_2 (and_2_out, not_5_out, e1, not_6_out);
  not not_6 (not_6_out, r0);
  and and_3 (and_3_out, e0, not_7_out, not_8_out);
  not not_7 (not_7_out, e1);
  not not_8 (not_8_out, r0);
  and and_4 (and_4_out, e0, e1, r0);
  and and_5 (and_5_out, not_1_out, e1, r0);
  and and_6 (and_6_out, e0, not_2_out, r0);
  and and_7 (and_7_out, e0, e1);
  or or_1 (s, and_1_out, and_2_out, and_3_out, and_4_out);
  or or_2 (r, and_5_out, and_6_out, and_7_out);
endmodule
