// Logisim project Circuit-1.circ as structural Verilog: 1 circuit, main circuit main
module main (
  input  x,
  input  y,
  input  z,
  output f_x_y_z
);

  wire and_1_out, not_1_out, or_1_out;

  not not_1 (not_1_out, y);
  and and_1 (and_1_out, x, y);
  or or_1 (or_1_out, not_1_out, z);
  xor xor_1 (f_x_y_z, and_1_out, or_1_out);
endmodule
