// Logisim project Decodeur.circ as structural Verilog: 1 circuit, main circuit main
module main (
  input  e1,
  input  e0,
  output s0,
  output s1,
  output s2,
  output s3
);

  wire not_1_out, not_2_out;

  not not_1 (not_1_out, e0);
  not not_2 (not_2_out, e1);
  and and_1 (s0, not_1_out, not_2_out);
  and and_2 (s1, e0, not_2_out);
  and and_3 (s2, not_1_out, e1);
  and and_4 (s3, e0, e1);
endmodule
