// Logisim project DemiAdditionneur.circ as structural Verilog: 1 circuit, main circuit main
module main (
  input  e0,
  input  e1,
  output s,
  output r
);

  wire and_1_out, and_2_out, not_1_out, not_2_out;

  not not_1 (not_1_out, e0);
  not not_2 (not_2_out, e1);
  and and_1 (and_1_out, not_1_out, e1);
  or or_1 (s, and_1_out, and_2_out);
  and and_2 (and_2_out, e0, not_2_out);
  and and_3 (r, e0, e1);
endmodule
