// Logisim project Multiplexeur.circ as structural Verilog: 1 circuit, main circuit main
module main (
  input  x,
  input  y,
  input  z,
  output M_x_y_z
);

  wire and_1_out, and_2_out, not_1_out;

  not not_1 (not_1_out, x);
  and and_1 (and_1_out, not_1_out, y);
  and and_2 (and_2_out, x, z);
  or or_1 (M_x_y_z, and_1_out, and_2_out);
endmodule
