// Logisim project NAND2.circ as structural Verilog: 1 circuit, main circuit main
module main (
  input  in_1,
  input  in_2
);

  wire transistor_1_out, transistor_3_out;

  Transistor #(.\type ("n")) transistor_1 (.in(transistor_3_out), .out(transistor_1_out), .gate(in_1));
  Transistor transistor_2 (.in(1'b1), .out(transistor_1_out), .gate(in_1));
  Transistor #(.\type ("n")) transistor_3 (.in(1'b0), .out(transistor_3_out), .gate(in_2));
  Transistor #(.gate("br")) transistor_4 (.in(1'b1), .out(transistor_1_out), .gate(in_2));
  // Probe on transistor_1_out
endmodule
