// Logisim project NOR2.circ as structural Verilog: 1 circuit, main circuit main
module main (
  input  in_1,
  input  in_2
);

  wire transistor_1_out, transistor_2_out;

  Transistor #(.\type ("n")) transistor_1 (.in(1'b0), .out(transistor_1_out), .gate(in_2));
  Transistor transistor_2 (.in(1'b1), .out(transistor_2_out), .gate(in_1));
  Transistor #(.\type ("n"), .gate("br")) transistor_3 (.in(1'b0), .out(transistor_1_out), .gate(in_1));
  // Probe on transistor_1_out
  Transistor transistor_4 (.in(transistor_2_out), .out(transistor_1_out), .gate(in_2));
endmodule
